# Fritzing sketch YooKBpy - wires (saved by Fritzing 0.9.3b)
circuit board: 10cm x 10cm

parts:
  A1 = Waveshare rp2040-zero smd [package=SMD]
  S1 = Cherry MX Blue [part_number=1]
  D1 = Diode [package=diode-1n4148]
  S2 = Cherry MX Blue
  S3 = Cherry MX Blue
  S4 = Cherry MX Blue
  S5 = Cherry MX Blue
  D2 = Diode [package=diode-1n4148]
  D3 = Diode [package=diode-1n4148]
  D4 = Diode [package=diode-1n4148]
  D5 = Diode [package=diode-1n4148]
  S6 = Cherry MX Blue
  S7 = Cherry MX Blue
  S8 = Cherry MX Blue
  S9 = Cherry MX Blue
  S10 = Cherry MX Blue
  D6 = Diode [package=diode-1n4148]
  D7 = Diode [package=diode-1n4148]
  D8 = Diode [package=diode-1n4148]
  D9 = Diode [package=diode-1n4148]
  D10 = Diode [package=diode-1n4148]
  S12 = Cherry MX Blue
  S13 = Cherry MX Blue
  S15 = Cherry MX Blue
  D11 = Diode [package=diode-1n4148]
  D12 = Diode [package=diode-1n4148]
  D15 = Diode [package=diode-1n4148]
  S16 = Cherry MX Blue
  S17 = Cherry MX Blue
  S18 = Cherry MX Blue
  S19 = Cherry MX Blue
  S20 = Cherry MX Blue
  D16 = Diode [package=diode-1n4148]
  D17 = Diode [package=diode-1n4148]
  D18 = Diode [package=diode-1n4148]
  D19 = Diode [package=diode-1n4148]
  D20 = Diode [package=diode-1n4148]
  LED1 = LED - 5mm [color="Blue (430nm)" package="5 mm [THT]"]
  LED2 = LED - 5mm [color="Blue (430nm)" package="5 mm [THT]"]
  LED3 = LED - 5mm [color="Blue (430nm)" package="5 mm [THT]"]
  LED4 = LED - 5mm [color="Blue (430nm)" package="5 mm [THT]"]
  LED5 = LED - 5mm [color="Blue (430nm)" package="5 mm [THT]"]
  Part1 = OLED Color 0.96 inch 96x64 w microSD [part_number=684]

nets:
  N1: A1.Pin_2, A1.Pin_33, LED1.cathode, LED2.cathode, LED3.cathode, LED4.cathode, LED5.cathode, Part1.GND
  N2: A1.Pin_3, Part1.V+
  N3: A1.Pin_5, Part1.RESET
  N4: A1.Pin_6, Part1.DC
  N5: A1.Pin_7, Part1.OLED_CS
  N6: A1.Pin_8, Part1.MOSI
  N7: A1.Pin_9, Part1.SCK
  N8: A1.Pin_10, LED5.anode
  N9: A1.Pin_11, LED4.anode
  N10: A1.Pin_12, LED3.anode
  N11: A1.Pin_13, LED2.anode
  N12: A1.Pin_14, LED1.anode
  N13: A1.Pin_15, D19.A
  N14: A1.Pin_16, D15.A
  N15: A1.Pin_17, D9.A
  N16: A1.Pin_18, D5.A
  N17: A1.Pin_19, S5.pin_2, S6.pin_2, S16.pin_2
  N18: A1.Pin_20, S4.pin_2, S10.pin_2, S15.pin_2, S20.pin_2
  N19: A1.Pin_21, S3.pin_2, S17.pin_2
  N20: A1.Pin_22, S2.pin_2, S18.pin_2
  N21: A1.Pin_23, S1.pin_2, S19.pin_2
  N22: S1.pin_1, D1.C
  N23: D1.A, S2.pin_1, D2.C
  N24: S3.pin_1, D2.A, D3.C
  N25: S4.pin_1, D3.A, D4.C
  N26: S5.pin_1, D4.A, D5.C
  N27: S6.pin_1, D9.C, D10.A
  N28: S7.pin_1, D6.A, D7.C
  N29: S8.pin_1, D6.C, D8.A
  N30: S9.pin_1, D8.C
  N31: S10.pin_1, D7.A, D10.C
  N32: S12.pin_1, D11.A, D12.C
  N33: S13.pin_1, D11.C
  N34: S15.pin_1, D12.A, D15.C
  N35: S16.pin_1, D19.C, D20.A
  N36: S17.pin_1, D16.A, D17.C
  N37: S18.pin_1, D16.C, D18.A
  N38: S19.pin_1, D18.C
  N39: S20.pin_1, D17.A, D20.C

custom parts:
  Waveshare rp2040-zero smd: .RP2040-Zero, A Low-Cost, High-Performance Pico-Like MCU Board Based On Raspberry Pi Microcontroller RP2040. This varant is SMD with all the connections.
  Cherry MX Blue: Cherry MX Blue Keyswitch button for keyboards
  OLED Color 0.96 inch 96x64 w microSD: The visible portion of this OLED measures 0.96" diagonal and contains 96x64 RGB pixels, each one made of red, green and blue OLEDs. Each pixel can be set with 16-bits of resolution for a large range of colors. Because the display uses OLEDs, there is no backlight, and the contrast is very high (black is really black). We picked this display for its excellent color, this is the nicest mini OLED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
